// Logisim project lab2.circ as structural Verilog: 11 circuits, main circuit main
module main (
  input  in_1,
  output [3:0] out_2
);

  wire Clock_out, global_1_s1, global_1_s2, global_1_s3, global_1_s4, Reset_out;

  Global global_1 (
    .X(in_1), .CLOCK(Clock_out), .RST(Reset_out), .s1(global_1_s1), .s2(global_1_s2), .s3(global_1_s3),
    .s4(global_1_s4), .out_4(out_2));
  Button Clock (.out(Clock_out));
  Button Reset (.out(Reset_out));
endmodule

module Secuencia_1 (
  input  X,
  input  RST,
  output S
);

  wire clock_1_out, not_1_out, not_2_out, not_3_out, Q0, Q1, R0, S1;

  not not_1 (not_1_out, Q1);
  not not_2 (not_2_out, X);
  not not_3 (not_3_out, X);
  and and_1 (S, Q1, Q0, X);
  and and_2 (S1, not_1_out, Q0, not_2_out);
  and and_3 (R0, Q1, not_3_out);
  Clock clock_1 (.out(clock_1_out));
  S_R_Flip_Flop s_r_ff_1 (.S(S1), .clk(clock_1_out), .R(Q1), .Q(Q1), .reset(RST));  // open: Qn, preset, en
  S_R_Flip_Flop s_r_ff_2 (.S(X), .clk(clock_1_out), .R(R0), .Q(Q0), .reset(RST));  // open: Qn, preset, en

  // Other names for the same wires on the sheet: R1 = Q1; S0 = X
endmodule

module Secuencia_2 (
  input  X,
  input  RST,
  output S
);

  wire and_1_out, and_2_out, clock_1_out, not_2_out, not_3_out, not_4_out, not_5_out, Q0, Q1, R0, R1, S0, S1;

  and and_1 (and_1_out, Q0, X);
  and and_2 (and_2_out, Q1, X);
  not not_1 (R1, X);
  not not_2 (not_2_out, Q1);
  not not_3 (not_3_out, X);
  not not_4 (not_4_out, Q0);
  not not_5 (not_5_out, X);
  or or_1 (S1, and_1_out, and_2_out);
  and and_3 (S0, not_2_out, X);
  or or_2 (R0, not_3_out, Q1);
  and and_4 (S, Q1, not_4_out, not_5_out);
  Clock clock_1 (.out(clock_1_out));
  S_R_Flip_Flop s_r_ff_1 (.S(S1), .clk(clock_1_out), .R(R1), .Q(Q1), .reset(RST));  // open: Qn, preset, en
  S_R_Flip_Flop s_r_ff_2 (.S(S0), .clk(clock_1_out), .R(R0), .Q(Q0), .reset(RST));  // open: Qn, preset, en
endmodule

module Secuencia_3 (
  input  X,
  input  RST,
  output S
);

  wire and_1_out, and_2_out, and_3_out, and_4_out, and_5_out, and_6_out, clock_1_out, not_1_out, not_2_out,
       not_3_out, not_4_out, not_5_out, not_6_out, not_7_out, not_8_out, not_9_out, not_10_out, Q0, Q1, Q2,
       R0, R1, S0, S1, S2;

  not not_1 (not_1_out, Q2);
  not not_2 (not_2_out, Q0);
  not not_3 (not_3_out, Q1);
  and and_1 (and_1_out, not_3_out, Q0, not_4_out);
  not not_4 (not_4_out, X);
  and and_2 (and_2_out, Q2, Q0);
  and and_3 (and_3_out, Q1, Q0, not_5_out);
  not not_5 (not_5_out, X);
  and and_4 (and_4_out, Q2, X);
  not not_6 (not_6_out, Q1);
  and and_5 (and_5_out, not_6_out, X);
  not not_7 (not_7_out, Q0);
  and and_6 (and_6_out, Q1, not_7_out, not_8_out);
  not not_8 (not_8_out, X);
  and and_7 (R0, Q1, Q0);
  not not_9 (not_9_out, Q0);
  not not_10 (not_10_out, X);
  and and_8 (S2, not_1_out, Q1, not_2_out, X);
  or or_1 (S1, and_1_out, and_2_out);
  or or_2 (R1, and_3_out, and_4_out);
  or or_3 (S0, and_5_out, and_6_out, Q2);
  and and_9 (S, Q2, Q1, not_9_out, not_10_out);
  Clock clock_1 (.out(clock_1_out));
  S_R_Flip_Flop s_r_ff_1 (.S(S2), .clk(clock_1_out), .R(Q2), .Q(Q2), .reset(RST));  // open: Qn, preset, en
  S_R_Flip_Flop s_r_ff_2 (.S(S1), .clk(clock_1_out), .R(R1), .Q(Q1), .reset(RST));  // open: Qn, preset, en
  S_R_Flip_Flop s_r_ff_3 (.S(S0), .clk(clock_1_out), .R(R0), .Q(Q0), .reset(RST));  // open: Qn, preset, en

  // Other names for the same wires on the sheet: R2 = Q2
endmodule

module Secuencia_4 (
  input  X,
  input  RST,
  output S
);

  wire and_2_out, and_3_out, and_4_out, and_5_out, and_6_out, and_7_out, and_8_out, and_9_out, and_10_out,
       clock_1_out, not_1_out, not_2_out, not_3_out, not_4_out, not_5_out, not_6_out, not_7_out, not_8_out,
       not_9_out, not_10_out, not_11_out, not_12_out, not_13_out, not_14_out, not_15_out, not_16_out,
       not_17_out, Q0, Q1, Q2, R0, R1, R2, S0, S1, S2;

  and and_1 (S2, Q1, Q0, X);
  not not_1 (not_1_out, Q1);
  or or_1 (R2, not_1_out, not_2_out);
  not not_2 (not_2_out, X);
  not not_3 (not_3_out, Q2);
  and and_2 (and_2_out, not_3_out, Q0, not_4_out);
  not not_4 (not_4_out, X);
  not not_5 (not_5_out, Q2);
  and and_3 (and_3_out, not_5_out, Q1, not_6_out);
  not not_6 (not_6_out, X);
  not not_7 (not_7_out, Q1);
  and and_4 (and_4_out, not_7_out, not_8_out);
  not not_8 (not_8_out, Q0);
  not not_9 (not_9_out, Q0);
  and and_5 (and_5_out, not_9_out, X);
  not not_10 (not_10_out, Q2);
  and and_6 (and_6_out, not_10_out, not_11_out, not_12_out);
  not not_11 (not_11_out, Q0);
  not not_12 (not_12_out, X);
  and and_7 (and_7_out, Q1, not_13_out);
  not not_13 (not_13_out, X);
  and and_8 (and_8_out, Q2, Q1);
  not not_14 (not_14_out, Q1);
  and and_9 (and_9_out, not_14_out, X);
  not not_15 (not_15_out, Q2);
  not not_16 (not_16_out, Q1);
  and and_10 (and_10_out, not_15_out, not_16_out, Q0);
  not not_17 (not_17_out, Q1);
  or or_2 (S1, and_2_out, and_3_out);
  or or_3 (R1, and_4_out, and_5_out, Q2);
  or or_4 (S0, and_6_out, and_7_out, and_8_out);
  or or_5 (R0, and_9_out, and_10_out);
  and and_11 (S, Q2, not_17_out, Q0, X);
  Clock clock_1 (.out(clock_1_out));
  S_R_Flip_Flop s_r_ff_1 (.S(S2), .clk(clock_1_out), .R(R2), .Q(Q2), .reset(RST));  // open: Qn, preset, en
  S_R_Flip_Flop s_r_ff_2 (.S(S1), .clk(clock_1_out), .R(R1), .Q(Q1), .reset(RST));  // open: Qn, preset, en
  S_R_Flip_Flop s_r_ff_3 (.S(S0), .clk(clock_1_out), .R(R0), .Q(Q0), .reset(RST));  // open: Qn, preset, en
endmodule

module Global (
  input  X,
  input  CLOCK,
  input  RST,
  output [3:0] out_4,
  output s1,
  output s2,
  output s3,
  output s4
);

  wire and_2_out, and_3_out, and_4_out, and_5_out, and_6_out, and_7_out, and_8_out, and_9_out, and_10_out,
       and_11_out, and_12_out, and_13_out, and_14_out, and_15_out, and_16_out, and_17_out, and_18_out,
       and_19_out, and_20_out, and_21_out, and_22_out, and_23_out, and_24_out, not_1_out, not_2_out,
       not_3_out, not_4_out, not_5_out, not_6_out, not_7_out, not_8_out, not_9_out, not_10_out, not_11_out,
       not_12_out, not_13_out, not_14_out, not_15_out, not_16_out, not_17_out, not_18_out, not_19_out,
       not_20_out, not_21_out, not_22_out, not_23_out, not_24_out, not_25_out, not_26_out, not_27_out,
       not_28_out, not_29_out, not_30_out, not_31_out, not_32_out, not_33_out, not_34_out, not_35_out,
       not_36_out, not_37_out, not_38_out, not_39_out, not_40_out, not_41_out, not_42_out, not_43_out,
       not_44_out, not_45_out, not_46_out, R1, R2, R3, R4, S1_t, S2_t, S3_t, S4_t;

  not not_1 (not_1_out, out_4[1]);
  not not_2 (not_2_out, out_4[0]);
  not not_3 (not_3_out, X);
  not not_4 (not_4_out, out_4[3]);
  not not_5 (not_5_out, X);
  not not_6 (not_6_out, out_4[0]);
  not not_7 (not_7_out, out_4[1]);
  not not_8 (not_8_out, X);
  not not_9 (not_9_out, out_4[1]);
  not not_10 (not_10_out, out_4[3]);
  not not_11 (not_11_out, out_4[1]);
  not not_12 (not_12_out, X);
  not not_13 (not_13_out, out_4[0]);
  not not_14 (not_14_out, out_4[3]);
  not not_15 (not_15_out, out_4[3]);
  not not_16 (not_16_out, X);
  not not_17 (not_17_out, out_4[1]);
  not not_18 (not_18_out, out_4[0]);
  not not_19 (not_19_out, out_4[1]);
  not not_20 (not_20_out, out_4[2]);
  not not_21 (not_21_out, out_4[0]);
  not not_22 (not_22_out, out_4[1]);
  not not_23 (not_23_out, out_4[0]);
  not not_24 (not_24_out, out_4[3]);
  not not_25 (not_25_out, out_4[3]);
  not not_26 (not_26_out, X);
  not not_27 (not_27_out, out_4[1]);
  not not_28 (not_28_out, out_4[3]);
  not not_29 (not_29_out, out_4[0]);
  not not_30 (not_30_out, out_4[3]);
  not not_31 (not_31_out, out_4[0]);
  not not_32 (not_32_out, X);
  not not_33 (not_33_out, out_4[0]);
  not not_34 (not_34_out, out_4[2]);
  not not_35 (not_35_out, out_4[0]);
  not not_36 (not_36_out, out_4[3]);
  and and_1 (s1, out_4[0], out_4[1], out_4[2], out_4[3], X);
  not not_37 (not_37_out, out_4[2]);
  not not_38 (not_38_out, out_4[3]);
  not not_39 (not_39_out, X);
  not not_40 (not_40_out, out_4[1]);
  not not_41 (not_41_out, out_4[3]);
  not not_42 (not_42_out, X);
  not not_43 (not_43_out, out_4[0]);
  not not_44 (not_44_out, out_4[1]);
  not not_45 (not_45_out, out_4[3]);
  and and_2 (and_2_out, not_1_out, out_4[2]);
  and and_3 (and_3_out, not_2_out, out_4[1], not_3_out);
  and and_4 (and_4_out, out_4[1], out_4[2], not_4_out, X);
  and and_5 (and_5_out, out_4[0], out_4[1], out_4[3], not_5_out);
  and and_6 (and_6_out, not_6_out, not_7_out, out_4[3], not_8_out);
  and and_7 (and_7_out, not_9_out, out_4[2], not_10_out);
  and and_8 (and_8_out, not_11_out, out_4[2], not_12_out);
  and and_9 (and_9_out, not_13_out, out_4[1], not_14_out);
  and and_10 (and_10_out, out_4[0], not_15_out, not_16_out);
  and and_11 (and_11_out, out_4[0], not_17_out, out_4[3], X);
  and and_12 (and_12_out, not_18_out, out_4[1]);
  and and_13 (and_13_out, out_4[1], out_4[2], X);
  and and_14 (and_14_out, not_19_out, not_20_out, X);
  and and_15 (and_15_out, not_21_out, not_22_out, out_4[3]);
  and and_16 (and_16_out, not_23_out, out_4[1], not_24_out);
  and and_17 (and_17_out, out_4[0], not_25_out, not_26_out);
  and and_18 (and_18_out, not_27_out, out_4[2], not_28_out, X);
  and and_19 (and_19_out, not_29_out, out_4[1], not_30_out);
  and and_20 (and_20_out, not_31_out, out_4[1], not_32_out);
  and and_21 (and_21_out, out_4[0], out_4[2], out_4[3], X);
  and and_22 (and_22_out, not_33_out, not_34_out);
  not not_46 (not_46_out, X);
  and and_23 (and_23_out, not_35_out, out_4[1], not_36_out);
  and and_24 (and_24_out, out_4[0], X);
  and and_25 (s2, out_4[0], out_4[1], not_37_out, not_38_out, not_39_out);
  and and_26 (s3, out_4[0], not_40_out, out_4[2], not_41_out, not_42_out);
  and and_27 (s4, not_43_out, not_44_out, out_4[2], not_45_out, X);
  or or_1 (S1_t, and_2_out, and_3_out);
  or or_2 (R1, and_4_out, and_5_out);
  or or_3 (S2_t, and_6_out, and_7_out, and_8_out, and_9_out, and_10_out, and_11_out);
  or or_4 (R2, and_12_out, and_13_out);
  or or_5 (S3_t, and_14_out, and_15_out, and_16_out, and_17_out);
  or or_6 (R3, and_18_out, and_19_out, and_20_out, and_21_out);
  or or_7 (S4_t, and_22_out, not_46_out);
  or or_8 (R4, and_23_out, and_24_out);
  S_R_Flip_Flop s_r_ff_1 (.S(S1_t), .clk(CLOCK), .R(R1), .Q(out_4[0]), .reset(RST));  // open: Qn, preset, en
  S_R_Flip_Flop s_r_ff_2 (.S(S2_t), .clk(CLOCK), .R(R2), .Q(out_4[1]), .reset(RST));  // open: Qn, preset, en
  S_R_Flip_Flop s_r_ff_3 (.S(S3_t), .clk(CLOCK), .R(R3), .Q(out_4[2]), .reset(RST));  // open: Qn, preset, en
  S_R_Flip_Flop s_r_ff_4 (.S(S4_t), .clk(CLOCK), .R(R4), .Q(out_4[3]), .reset(RST));  // open: Qn, preset, en

  // Other names for the same wires on the sheet: Q1 = out_4[0]; Q2 = out_4[1]; Q3 = out_4[2]; Q4 = out_4[3]
endmodule

module Secuencia_1_COPIA (
  input  Q1,
  input  Q0,
  input  X,
  output S1,
  output R1,
  output S0,
  output R0,
  output S
);

  wire not_1_out, not_2_out, not_3_out;

  not not_1 (not_1_out, Q1);
  not not_2 (not_2_out, X);
  not not_3 (not_3_out, X);
  and and_1 (S, Q1, Q0, X);
  and and_2 (S1, not_1_out, Q0, not_2_out);
  and and_3 (R0, Q1, not_3_out);

  assign R1 = Q1;
  assign S0 = X;
endmodule

module Secuencia_2_COPIA (
  input  Q1,
  input  Q0,
  input  X,
  output S1,
  output R1,
  output S0,
  output R0,
  output S
);

  wire and_1_out, and_2_out, not_2_out, not_3_out, not_4_out, not_5_out;

  and and_1 (and_1_out, Q0, X);
  and and_2 (and_2_out, Q1, X);
  not not_1 (R1, X);
  not not_2 (not_2_out, Q1);
  not not_3 (not_3_out, X);
  not not_4 (not_4_out, Q0);
  not not_5 (not_5_out, X);
  or or_1 (S1, and_1_out, and_2_out);
  and and_3 (S0, not_2_out, X);
  or or_2 (R0, not_3_out, Q1);
  and and_4 (S, Q1, not_4_out, not_5_out);
endmodule

module Secuencia_3_COPIA (
  input  Q2,
  input  Q1,
  input  Q0,
  input  X,
  output S2,
  output R2,
  output S1,
  output R1,
  output S0,
  output R0,
  output S
);

  wire and_1_out, and_2_out, and_3_out, and_4_out, and_5_out, and_6_out, not_1_out, not_2_out, not_3_out,
       not_4_out, not_5_out, not_6_out, not_7_out, not_8_out, not_9_out, not_10_out;

  not not_1 (not_1_out, Q2);
  not not_2 (not_2_out, Q0);
  not not_3 (not_3_out, Q1);
  and and_1 (and_1_out, not_3_out, Q0, not_4_out);
  not not_4 (not_4_out, X);
  and and_2 (and_2_out, Q2, Q0);
  and and_3 (and_3_out, Q1, Q0, not_5_out);
  not not_5 (not_5_out, X);
  and and_4 (and_4_out, Q2, X);
  not not_6 (not_6_out, Q1);
  and and_5 (and_5_out, not_6_out, X);
  not not_7 (not_7_out, Q0);
  and and_6 (and_6_out, Q1, not_7_out, not_8_out);
  not not_8 (not_8_out, X);
  and and_7 (R0, Q1, Q0);
  not not_9 (not_9_out, Q0);
  not not_10 (not_10_out, X);
  and and_8 (S2, not_1_out, Q1, not_2_out, X);
  or or_1 (S1, and_1_out, and_2_out);
  or or_2 (R1, and_3_out, and_4_out);
  or or_3 (S0, and_5_out, and_6_out, Q2);
  and and_9 (S, Q2, Q1, not_9_out, not_10_out);

  assign R2 = Q2;
endmodule

module Secuencia_4_COPIA (
  input  Q2,
  input  Q1,
  input  Q0,
  input  X,
  output S2,
  output R2,
  output S1,
  output R1,
  output S0,
  output R0,
  output S
);

  wire and_2_out, and_3_out, and_4_out, and_5_out, and_6_out, and_7_out, and_8_out, and_9_out, and_10_out,
       not_1_out, not_2_out, not_3_out, not_4_out, not_5_out, not_6_out, not_7_out, not_8_out, not_9_out,
       not_10_out, not_11_out, not_12_out, not_13_out, not_14_out, not_15_out, not_16_out, not_17_out;

  and and_1 (S2, Q1, Q0, X);
  not not_1 (not_1_out, Q1);
  or or_1 (R2, not_1_out, not_2_out);
  not not_2 (not_2_out, X);
  not not_3 (not_3_out, Q2);
  and and_2 (and_2_out, not_3_out, Q0, not_4_out);
  not not_4 (not_4_out, X);
  not not_5 (not_5_out, Q2);
  and and_3 (and_3_out, not_5_out, Q1, not_6_out);
  not not_6 (not_6_out, X);
  not not_7 (not_7_out, Q1);
  and and_4 (and_4_out, not_7_out, not_8_out);
  not not_8 (not_8_out, Q0);
  not not_9 (not_9_out, Q0);
  and and_5 (and_5_out, not_9_out, X);
  not not_10 (not_10_out, Q2);
  not not_11 (not_11_out, Q0);
  and and_6 (and_6_out, not_10_out, not_11_out, not_12_out);
  not not_12 (not_12_out, X);
  and and_7 (and_7_out, Q1, not_13_out);
  not not_13 (not_13_out, X);
  and and_8 (and_8_out, Q2, Q1);
  not not_14 (not_14_out, Q1);
  and and_9 (and_9_out, not_14_out, X);
  not not_15 (not_15_out, Q2);
  not not_16 (not_16_out, Q1);
  and and_10 (and_10_out, not_15_out, not_16_out, Q0);
  not not_17 (not_17_out, Q1);
  or or_2 (S1, and_2_out, and_3_out);
  or or_3 (R1, and_4_out, and_5_out, Q2);
  or or_4 (S0, and_6_out, and_7_out, and_8_out);
  or or_5 (R0, and_9_out, and_10_out);
  and and_11 (S, Q2, not_17_out, Q0, X);
endmodule

module Global__Copia (
  input  Q1,
  input  Q2,
  input  Q3,
  input  Q4,
  input  X,
  output S1,
  output R1,
  output S2,
  output R2,
  output S3,
  output R3,
  output S4,
  output R4,
  output s1_2,
  output s2_2,
  output s3_2,
  output s4_2
);

  wire and_2_out, and_3_out, and_4_out, and_5_out, and_6_out, and_7_out, and_8_out, and_9_out, and_10_out,
       and_11_out, and_12_out, and_13_out, and_14_out, and_15_out, and_16_out, and_17_out, and_18_out,
       and_19_out, and_20_out, and_21_out, and_22_out, and_23_out, and_24_out, not_1_out, not_2_out,
       not_3_out, not_4_out, not_5_out, not_6_out, not_7_out, not_8_out, not_9_out, not_10_out, not_11_out,
       not_12_out, not_13_out, not_14_out, not_15_out, not_16_out, not_17_out, not_18_out, not_19_out,
       not_20_out, not_21_out, not_22_out, not_23_out, not_24_out, not_25_out, not_26_out, not_27_out,
       not_28_out, not_29_out, not_30_out, not_31_out, not_32_out, not_33_out, not_34_out, not_35_out,
       not_36_out, not_37_out, not_38_out, not_39_out, not_40_out, not_41_out, not_42_out, not_43_out,
       not_44_out, not_45_out, not_46_out;

  not not_1 (not_1_out, Q2);
  not not_2 (not_2_out, Q1);
  not not_3 (not_3_out, X);
  not not_4 (not_4_out, Q4);
  not not_5 (not_5_out, X);
  not not_6 (not_6_out, Q1);
  not not_7 (not_7_out, Q2);
  not not_8 (not_8_out, X);
  not not_9 (not_9_out, Q2);
  not not_10 (not_10_out, Q4);
  not not_11 (not_11_out, Q2);
  not not_12 (not_12_out, X);
  not not_13 (not_13_out, Q1);
  not not_14 (not_14_out, Q4);
  not not_15 (not_15_out, Q4);
  not not_16 (not_16_out, X);
  not not_17 (not_17_out, Q2);
  not not_18 (not_18_out, Q1);
  not not_19 (not_19_out, Q2);
  not not_20 (not_20_out, Q3);
  not not_21 (not_21_out, Q1);
  not not_22 (not_22_out, Q2);
  not not_23 (not_23_out, Q1);
  not not_24 (not_24_out, Q4);
  not not_25 (not_25_out, Q4);
  not not_26 (not_26_out, X);
  not not_27 (not_27_out, Q2);
  not not_28 (not_28_out, Q4);
  not not_29 (not_29_out, Q1);
  not not_30 (not_30_out, Q4);
  not not_31 (not_31_out, Q1);
  not not_32 (not_32_out, X);
  not not_33 (not_33_out, Q1);
  not not_34 (not_34_out, Q3);
  not not_35 (not_35_out, Q1);
  not not_36 (not_36_out, Q4);
  and and_1 (s1_2, Q1, Q2, Q3, Q4, X);
  not not_37 (not_37_out, Q3);
  not not_38 (not_38_out, Q4);
  not not_39 (not_39_out, X);
  not not_40 (not_40_out, Q2);
  not not_41 (not_41_out, Q4);
  not not_42 (not_42_out, X);
  not not_43 (not_43_out, Q1);
  not not_44 (not_44_out, Q2);
  not not_45 (not_45_out, Q4);
  and and_2 (and_2_out, not_1_out, Q3);
  and and_3 (and_3_out, not_2_out, Q2, not_3_out);
  and and_4 (and_4_out, Q2, Q3, not_4_out, X);
  and and_5 (and_5_out, Q1, Q2, Q4, not_5_out);
  and and_6 (and_6_out, not_6_out, not_7_out, Q4, not_8_out);
  and and_7 (and_7_out, not_9_out, Q3, not_10_out);
  and and_8 (and_8_out, not_11_out, Q3, not_12_out);
  and and_9 (and_9_out, not_13_out, Q2, not_14_out);
  and and_10 (and_10_out, Q1, not_15_out, not_16_out);
  and and_11 (and_11_out, Q1, not_17_out, Q4, X);
  and and_12 (and_12_out, not_18_out, Q2);
  and and_13 (and_13_out, Q2, Q3, X);
  and and_14 (and_14_out, not_19_out, not_20_out, X);
  and and_15 (and_15_out, not_21_out, not_22_out, Q4);
  and and_16 (and_16_out, not_23_out, Q2, not_24_out);
  and and_17 (and_17_out, Q1, not_25_out, not_26_out);
  and and_18 (and_18_out, not_27_out, Q3, not_28_out, X);
  and and_19 (and_19_out, not_29_out, Q2, not_30_out);
  and and_20 (and_20_out, not_31_out, Q2, not_32_out);
  and and_21 (and_21_out, Q1, Q3, Q4, X);
  and and_22 (and_22_out, not_33_out, not_34_out);
  not not_46 (not_46_out, X);
  and and_23 (and_23_out, not_35_out, Q2, not_36_out);
  and and_24 (and_24_out, Q1, X);
  and and_25 (s2_2, Q1, Q2, not_37_out, not_38_out, not_39_out);
  and and_26 (s3_2, Q1, not_40_out, Q3, not_41_out, not_42_out);
  and and_27 (s4_2, not_43_out, not_44_out, Q3, not_45_out, X);
  or or_1 (S1, and_2_out, and_3_out);
  or or_2 (R1, and_4_out, and_5_out);
  or or_3 (S2, and_6_out, and_7_out, and_8_out, and_9_out, and_10_out, and_11_out);
  or or_4 (R2, and_12_out, and_13_out);
  or or_5 (S3, and_14_out, and_15_out, and_16_out, and_17_out);
  or or_6 (R3, and_18_out, and_19_out, and_20_out, and_21_out);
  or or_7 (S4, and_22_out, not_46_out);
  or or_8 (R4, and_23_out, and_24_out);
endmodule
